// Logisim project 1byte.circ as structural Verilog
module Gates (
  input  in_1,
  input  in_2,
  input  in_3,
  input  in_4,
  input  in_5
);

  wire and_1_out, nand_1_out, not_1_out;

  nand nand_1 (nand_1_out, in_1, in_2);
  not not_1 (not_1_out, in_3);
  and and_1 (and_1_out, in_4, in_5);
  LED led_1 (.in(not_1_out));
  LED led_2 (.in(and_1_out));
  LED led_3 (.in(nand_1_out));

  // Notes on the sheet:
  //   1. GATES
  //   NOT GATE :
  //   NAND GATE : You get 0 when both inputs are ON
  //   AND GATE : You get 1when both inputs are ON
endmodule

module MemmoryBit (
  input  INPUT_BIT,
  input  THE_SET_BIT,
  input  in_3,
  input  MSB,
  input  in_5,
  input  in_6,
  input  in_7,
  input  in_8,
  input  in_9,
  input  in_10,
  input  LSB,
  input  in_12
);

  wire and_1_out, and_2_out, and_3_out, and_4_out, and_5_out, and_6_out, and_7_out, and_8_out, nand_1_out,
       nand_2_out, nand_3_out, nand_4_out, nand_5_out, nand_6_out, nand_7_out, nand_8_out, nand_9_out,
       nand_10_out, nand_11_out, nand_12_out, nand_13_out, nand_14_out, nand_15_out, nand_16_out,
       nand_17_out, nand_18_out, nand_19_out, nand_20_out, nand_21_out, nand_22_out, nand_23_out,
       nand_24_out, nand_25_out, nand_26_out, nand_27_out, nand_28_out, nand_29_out, nand_30_out,
       nand_31_out, nand_32_out, nand_33_out, nand_34_out, nand_35_out, nand_36_out;

  nand nand_1 (nand_1_out, INPUT_BIT, THE_SET_BIT);
  nand nand_2 (nand_2_out, nand_1_out, THE_SET_BIT);
  nand nand_3 (nand_3_out, nand_1_out, nand_4_out);
  nand nand_4 (nand_4_out, nand_3_out, nand_2_out);
  nand nand_5 (nand_5_out, in_9, in_12);
  nand nand_6 (nand_6_out, in_10, in_12);
  nand nand_7 (nand_7_out, LSB, in_12);
  LED led_1 (.in(nand_3_out));
  nand nand_8 (nand_8_out, MSB, in_12);
  nand nand_9 (nand_9_out, in_5, in_12);
  nand nand_10 (nand_10_out, in_6, in_12);
  nand nand_11 (nand_11_out, in_7, in_12);
  nand nand_12 (nand_12_out, in_8, in_12);
  nand nand_13 (nand_13_out, nand_5_out, in_12);
  nand nand_14 (nand_14_out, nand_6_out, in_12);
  nand nand_15 (nand_15_out, nand_7_out, in_12);
  nand nand_16 (nand_16_out, nand_8_out, in_12);
  nand nand_17 (nand_17_out, nand_9_out, in_12);
  nand nand_18 (nand_18_out, nand_10_out, in_12);
  nand nand_19 (nand_19_out, nand_11_out, in_12);
  nand nand_20 (nand_20_out, nand_12_out, in_12);
  nand nand_21 (nand_21_out, nand_10_out, nand_22_out);
  nand nand_22 (nand_22_out, nand_21_out, nand_18_out);
  nand nand_23 (nand_23_out, nand_11_out, nand_24_out);
  nand nand_24 (nand_24_out, nand_23_out, nand_19_out);
  nand nand_25 (nand_25_out, nand_12_out, nand_26_out);
  nand nand_26 (nand_26_out, nand_25_out, nand_20_out);
  nand nand_27 (nand_27_out, nand_5_out, nand_28_out);
  nand nand_28 (nand_28_out, nand_27_out, nand_13_out);
  nand nand_29 (nand_29_out, nand_6_out, nand_30_out);
  nand nand_30 (nand_30_out, nand_29_out, nand_14_out);
  nand nand_31 (nand_31_out, nand_7_out, nand_32_out);
  nand nand_32 (nand_32_out, nand_31_out, nand_15_out);
  nand nand_33 (nand_33_out, nand_8_out, nand_34_out);
  nand nand_34 (nand_34_out, nand_33_out, nand_16_out);
  nand nand_35 (nand_35_out, nand_9_out, nand_36_out);
  nand nand_36 (nand_36_out, nand_35_out, nand_17_out);
  LedBar ledbar_1 (
    .led0(nand_33_out), .led1(nand_35_out), .led2(nand_21_out), .led3(nand_23_out), .led4(nand_25_out),
    .led5(nand_27_out), .led6(nand_29_out), .led7(nand_31_out));
  and and_1 (and_1_out, nand_33_out, in_3);
  and and_2 (and_2_out, nand_35_out, in_3);
  and and_3 (and_3_out, nand_21_out, in_3);
  and and_4 (and_4_out, nand_23_out, in_3);
  and and_5 (and_5_out, nand_25_out, in_3);
  and and_6 (and_6_out, nand_27_out, in_3);
  and and_7 (and_7_out, nand_29_out, in_3);
  and and_8 (and_8_out, nand_31_out, in_3);
  LedBar ledbar_2 (
    .led0(and_1_out), .led1(and_2_out), .led2(and_3_out), .led3(and_4_out), .led4(and_5_out),
    .led5(and_6_out), .led6(and_7_out), .led7(and_8_out));

  // Notes on the sheet:
  //   INPUT BYTE
  //   Set Bit
  //   A
  //   PUT 8 of these together  and you get a byte of memmory
  //   THIS COMBINATION OF GATES HAVE THE ABILITY TO  HOLD ONTO THE INPUT BIT
  //   B
  //   INPUT BIT
  //   INPUT BIT
  //   INPUT BIT
  //   INPUT BIT
  //   OUTPUT BIT
  //   A
  //   A
  //   A
  //   A
  //   A
  //   B
  //   A
  //   B
  //   A
  //   B
  //   A
  //   B
  //   B
  //   B
  //   B
  //   B
  //   OUTPUT BIT
  //   OUTPUT BIT
  //   OUTPUT BIT
  //   Enable onto the  BUS ?
endmodule
